// Logisim project simon_says_reduce_5_logic_dia.circ as structural Verilog: 1 circuit, main circuit main
// 3
module main (
);

  wire and_1_out, and_2_out, and_3_out, and_4_out, and_5_out, and_6_out, and_7_out, and_8_out, and_9_out,
       and_10_out, and_11_out, and_12_out, and_13_out, and_14_out, and_15_out, and_16_out, and_17_out,
       button_5_out, button_7_out, button_8_out, button_9_out, clock_1_out, clock_2_out, clock_3_out,
       clock_4_out, d_ff_1_q, d_ff_2_q, d_ff_3_q, d_ff_4_q, d_ff_5_q, d_ff_6_q, d_ff_7_q, d_ff_8_q, d_ff_9_q,
       demultiplexer_6_out0, demultiplexer_6_out6, demultiplexer_6_out7, dipswitch_1_p1, dipswitch_1_p2,
       dipswitch_1_p3, dipswitch_1_p4, dipswitch_2_p1, dipswitch_2_p2, dipswitch_2_p3, dipswitch_2_p4,
       j_k_ff_1_q, multiplexer_1_out, multiplexer_2_out, multiplexer_3_out, multiplexer_4_out,
       multiplexer_5_out, multiplexer_6_out, multiplexer_7_out, multiplexer_8_out, multiplexer_9_out,
       multiplexer_10_out, n74175_1_pin1, n74175_1_pin2, n74175_1_pin4, n74175_1_pin5, n74175_1_pin7,
       n74175_1_pin9, n74175_1_pin10, n74175_1_pin12, n74175_1_pin13, n74175_1_pin15, n74175_2_pin2,
       n74175_2_pin4, n74175_2_pin5, n74175_2_pin7, n74175_2_pin9, n74175_2_pin10, n74175_2_pin12,
       n74175_2_pin13, n74175_2_pin15, n74175_3_pin2, n74175_3_pin4, n74175_3_pin5, n74175_3_pin7,
       n74175_3_pin9, n74175_3_pin10, n74175_3_pin12, n74175_3_pin13, n74175_3_pin15, n74175_4_pin2,
       n74175_4_pin4, n74175_4_pin5, n74175_4_pin7, n74175_4_pin9, n74175_4_pin10, n74175_4_pin12,
       n74175_4_pin13, n74175_4_pin15, n74175_5_pin2, n74175_5_pin4, n74175_5_pin5, n74175_5_pin7,
       n74175_5_pin9, n74175_5_pin10, n74175_5_pin12, n74175_5_pin13, n74175_5_pin15, nor_1_out, not_1_out,
       not_2_out, not_3_out, not_4_out, not_5_out, not_6_out, or_1_out, or_2_out, or_3_out, or_4_out,
       or_5_out, or_6_out, or_7_out, or_10_out, or_11_out, or_12_out, register_1_q, register_2_q,
       register_3_q, register_4_q, register_5_q, register_6_q, register_7_q, register_8_q, xnor_1_out,
       xnor_2_out, xnor_3_out, xnor_4_out, xnor_5_out, xnor_6_out, xnor_7_out;
  wire [0:0] button_10_out;
  wire [1:0] random_1_out;
  wire [2:0] counter_1_q, counter_2_q, counter_3_q, or_8_out, register_9_q;

  Clock clock_1 (.out(clock_1_out));
  Clock clock_2 (.out(clock_2_out));
  D_Flip_Flop d_ff_1 (.D(j_k_ff_1_q), .clk(j_k_ff_1_q), .Q(d_ff_1_q), .reset(and_5_out));  // open: Qn, preset
  Register #(.width(1)) register_1 (.D(dipswitch_1_p1), .en(1'b1), .clk(clock_1_out), .Q(register_1_q), .clr(1'b0));
  Register #(.width(1)) register_2 (.D(dipswitch_2_p1), .en(1'b1), .clk(clock_2_out), .Q(register_2_q), .clr(1'b0));
  or or_1 (or_1_out, and_7_out, button_9_out);
  not not_1 (not_1_out, d_ff_2_q);
  D_Flip_Flop d_ff_2 (.D(or_1_out), .clk(or_1_out), .Q(d_ff_2_q), .reset(and_5_out));  // open: Qn, preset
  and and_1 (and_1_out, d_ff_1_q, clock_3_out);
  or or_2 (or_2_out, or_1_out, button_9_out);
  and and_2 (and_2_out, d_ff_2_q, and_1_out);
  and and_3 (and_3_out, and_2_out, not_3_out);
  Clock clock_3 (.out(clock_3_out));
  // DipSwitch #(.number(4)) dipswitch_1: pin names not known; wires that end beside it: dipswitch_1_p1, dipswitch_1_p2, dipswitch_1_p3, dipswitch_1_p4
  // DipSwitch #(.number(4)) dipswitch_2: pin names not known; wires that end beside it: dipswitch_2_p1, dipswitch_2_p2, dipswitch_2_p3, dipswitch_2_p4
  or or_3 (or_3_out, or_1_out, and_2_out);
  D_Flip_Flop d_ff_3 (.D(and_3_out), .clk(and_3_out), .Q(d_ff_3_q), .reset(and_5_out));  // open: Qn, preset
  D_Flip_Flop d_ff_4 (.D(or_2_out), .clk(or_2_out), .Q(d_ff_4_q), .reset(and_5_out));  // open: Qn, preset
  Register #(.width(1)) register_3 (.D(dipswitch_1_p2), .en(1'b1), .clk(clock_1_out), .Q(register_3_q), .clr(1'b0));
  xnor xnor_1 (xnor_1_out, register_1_q, register_2_q);
  Register #(.width(1)) register_4 (.D(dipswitch_2_p2), .en(1'b1), .clk(clock_2_out), .Q(register_4_q), .clr(1'b0));
  and and_4 (and_4_out, not_2_out, and_7_out);
  not not_2 (not_2_out, button_10_out[0]);
  Counter #(.max('h7), .width(3)) counter_1 (
    .clr(and_5_out), .load(or_1_out), .count(or_3_out), .clk(or_3_out), .Q(counter_1_q));  // open: up, D, carry
  D_Flip_Flop #(.trigger("falling")) d_ff_5 (
    .D(d_ff_3_q), .clk(and_3_out), .Q(d_ff_5_q), .reset(and_5_out));  // open: Qn, preset
  J_K_Flip_Flop #(.trigger("falling")) j_k_ff_1 (
    .J(d_ff_4_q), .K(d_ff_4_q), .clk(clock_3_out), .Q(j_k_ff_1_q), .reset(and_5_out));  // open: Qn, preset
  not not_3 (not_3_out, d_ff_5_q);
  xnor xnor_2 (xnor_2_out, register_3_q, register_4_q);
  Register #(.width(1)) register_5 (.D(dipswitch_2_p3), .en(1'b1), .clk(clock_2_out), .Q(register_5_q), .clr(1'b0));
  or or_4 (or_4_out, button_10_out[0], or_12_out);
  and and_5 (and_5_out, d_ff_5_q, not_4_out);
  not not_4 (not_4_out, or_11_out);
  Register #(.width(1)) register_6 (.D(dipswitch_1_p3), .en(1'b1), .clk(clock_1_out), .Q(register_6_q), .clr(1'b0));
  and and_6 (and_6_out, xnor_2_out, xnor_1_out);
  Counter #(.max('h7), .width(3)) counter_2 (
    .load(button_10_out[0]), .count(1'b1), .clk(or_4_out), .D({2'b00, button_10_out[0]}), .Q(counter_2_q));  // open: clr, up, carry
  and and_7 (and_7_out, xnor_4_out, xnor_5_out, xnor_7_out);
  D_Flip_Flop d_ff_6 (.D(and_10_out), .clk(d_ff_8_q), .Q(d_ff_6_q), .reset(or_5_out));  // open: Qn, preset
  Counter #(.max('h7), .width(3)) counter_3 (
    .clr(or_7_out), .up(d_ff_6_q), .count(d_ff_6_q), .clk(d_ff_6_q), .Q(counter_3_q));  // open: load, D, carry
  Button button_1 ();  // open: out
  Button button_2 ();  // open: out
  Button button_3 ();  // open: out
  or or_5 (or_5_out, d_ff_6_q, button_10_out[0]);
  Button button_4 (.out(or_8_out[2]));
  Button button_5 (.out(button_5_out));
  Register #(.width(1)) register_7 (.D(dipswitch_1_p4), .en(1'b1), .clk(clock_1_out), .Q(register_7_q), .clr(1'b0));
  xnor xnor_3 (xnor_3_out, register_6_q, register_5_q);
  Register #(.width(1)) register_8 (.D(dipswitch_2_p4), .en(1'b1), .clk(clock_2_out), .Q(register_8_q), .clr(1'b0));
  Button button_6 ();  // open: out
  D_Flip_Flop d_ff_7 (.D(and_9_out), .clk(and_9_out), .Q(d_ff_7_q), .reset(or_5_out));  // open: Qn, preset
  Button button_7 (.out(button_7_out));
  Button button_8 (.out(button_8_out));
  and and_8 (and_8_out, xnor_3_out, and_6_out);
  xnor xnor_4 (xnor_4_out, counter_2_q[0], counter_3_q[0]);
  or or_6 (or_6_out, button_7_out, button_8_out, button_5_out, or_8_out[2]);
  and and_9 (and_9_out, not_1_out, or_6_out);
  D_Flip_Flop #(.trigger("falling")) d_ff_8 (
    .D(d_ff_7_q), .clk(and_9_out), .Q(d_ff_8_q), .reset(or_5_out));  // open: Qn, preset
  and and_10 (and_10_out, d_ff_7_q, and_11_out);
  LED led_1 (.in(and_10_out));
  xnor xnor_5 (xnor_5_out, counter_2_q[1], counter_3_q[1]);
  Hex_Digit_Display hex_digit_display_1 (.value({1'b0, counter_2_q}));  // open: dp
  xnor xnor_6 (xnor_6_out, register_7_q, register_8_q);
  or or_7 (or_7_out, and_7_out, button_9_out);
  D_Flip_Flop d_ff_9 (
    .D(multiplexer_1_out), .clk(multiplexer_1_out), .Q(d_ff_9_q), .reset(or_5_out));  // open: Qn, preset
  and and_11 (and_11_out, d_ff_7_q, d_ff_9_q);
  not not_5 (not_5_out, and_11_out);
  and and_12 (and_12_out, d_ff_7_q, not_5_out);
  LED led_2 (.in(and_12_out));
  LED led_3 (.in(and_17_out));
  and and_13 (and_13_out, xnor_6_out, and_8_out);
  xnor xnor_7 (xnor_7_out, counter_2_q[2], counter_3_q[2]);
  or or_8 (or_8_out[0], button_7_out, button_5_out);
  or or_9 (or_8_out[1], button_8_out, button_5_out);
  and and_14 (and_14_out, and_2_out, multiplexer_7_out);
  LED led_4 (.in(and_14_out));
  LED led_5 (.in(and_16_out));
  LED led_6 (.in(and_13_out));
  LED led_7 (.in(and_15_out));
  Button button_9 (.out(button_9_out));
  and and_15 (and_15_out, and_2_out, multiplexer_8_out);
  buf or_10 (or_10_out, and_4_out);  // OR_Gate
  not not_6 (not_6_out, d_ff_7_q);
  Button button_10 (.out(button_10_out[0]));
  Register #(.width(3)) register_9 (.D(or_8_out), .en(not_6_out), .clk(or_6_out), .Q(register_9_q), .clr(or_5_out));
  and and_16 (and_16_out, and_2_out, multiplexer_9_out);
  and and_17 (and_17_out, and_2_out, multiplexer_10_out);
  Multiplexer #(.select(3)) multiplexer_1 (
    .in0(multiplexer_2_out), .in1(multiplexer_3_out), .in2(multiplexer_4_out), .in3(multiplexer_5_out),
    .in4(multiplexer_6_out), .in5(1'b0), .in6(1'b0), .in7(1'b0), .out(multiplexer_1_out), .sel(counter_3_q));
  or or_11 (or_11_out, multiplexer_10_out, multiplexer_9_out, multiplexer_8_out, multiplexer_7_out);
  Multiplexer #(.select(3)) multiplexer_2 (
    .in0(1'b0), .in1(n74175_1_pin7), .in2(n74175_1_pin2), .in3(n74175_1_pin15), .in4(n74175_1_pin10),
    .out(multiplexer_2_out), .sel(register_9_q));  // open: in5, in6, in7
  Multiplexer #(.select(3)) multiplexer_3 (
    .in0(1'b0), .in1(n74175_2_pin7), .in2(n74175_2_pin2), .in3(n74175_2_pin15), .in4(n74175_2_pin10),
    .out(multiplexer_3_out), .sel(register_9_q));  // open: in5, in6, in7
  Multiplexer #(.select(3)) multiplexer_4 (
    .in0(1'b0), .in1(n74175_3_pin7), .in2(n74175_3_pin2), .in3(n74175_3_pin15), .in4(n74175_3_pin10),
    .out(multiplexer_4_out), .sel(register_9_q));  // open: in5, in6, in7
  Multiplexer #(.select(3)) multiplexer_5 (
    .in0(1'b0), .in1(n74175_4_pin7), .in2(n74175_4_pin2), .in3(n74175_4_pin15), .in4(n74175_4_pin10),
    .out(multiplexer_5_out), .sel(register_9_q));  // open: in5, in6, in7
  Multiplexer #(.select(3)) multiplexer_6 (
    .in0(1'b0), .in1(n74175_5_pin7), .in2(n74175_5_pin2), .in3(n74175_5_pin15), .in4(n74175_5_pin10),
    .out(multiplexer_6_out), .sel(register_9_q));  // open: in5, in6, in7
  nor nor_1 (nor_1_out, n74175_1_pin10, n74175_1_pin15, n74175_1_pin2, n74175_1_pin7);
  _74175 u_74175_1 (
    .pin1(n74175_1_pin1), .pin2(n74175_1_pin2), .pin4(n74175_1_pin4), .pin5(n74175_1_pin5),
    .pin7(n74175_1_pin7), .pin15(n74175_1_pin15), .pin13(n74175_1_pin13), .pin12(n74175_1_pin12),
    .pin10(n74175_1_pin10), .pin9(n74175_1_pin9));  // open: pin3, pin6, pin14, pin11
  _74175 u_74175_2 (
    .pin1(n74175_1_pin1), .pin2(n74175_2_pin2), .pin4(n74175_2_pin4), .pin5(n74175_2_pin5),
    .pin7(n74175_2_pin7), .pin15(n74175_2_pin15), .pin13(n74175_2_pin13), .pin12(n74175_2_pin12),
    .pin10(n74175_2_pin10), .pin9(n74175_2_pin9));  // open: pin3, pin6, pin14, pin11
  _74175 u_74175_3 (
    .pin1(n74175_1_pin1), .pin2(n74175_3_pin2), .pin4(n74175_3_pin4), .pin5(n74175_3_pin5),
    .pin7(n74175_3_pin7), .pin15(n74175_3_pin15), .pin13(n74175_3_pin13), .pin12(n74175_3_pin12),
    .pin10(n74175_3_pin10), .pin9(n74175_3_pin9));  // open: pin3, pin6, pin14, pin11
  _74175 u_74175_4 (
    .pin1(n74175_1_pin1), .pin2(n74175_4_pin2), .pin4(n74175_4_pin4), .pin5(n74175_4_pin5),
    .pin7(n74175_4_pin7), .pin15(n74175_4_pin15), .pin13(n74175_4_pin13), .pin12(n74175_4_pin12),
    .pin10(n74175_4_pin10), .pin9(n74175_4_pin9));  // open: pin3, pin6, pin14, pin11
  _74175 u_74175_5 (
    .pin1(n74175_1_pin1), .pin2(n74175_5_pin2), .pin4(n74175_5_pin4), .pin5(n74175_5_pin5),
    .pin7(n74175_5_pin7), .pin15(n74175_5_pin15), .pin13(n74175_5_pin13), .pin12(n74175_5_pin12),
    .pin10(n74175_5_pin10), .pin9(n74175_5_pin9));  // open: pin3, pin6, pin14, pin11
  and and_18 (n74175_1_pin9, nor_1_out, button_9_out);
  not not_7 (n74175_1_pin1, button_10_out[0]);
  Demultiplexer #(.select(2)) demultiplexer_1 (
    .out0(n74175_1_pin13), .out1(n74175_1_pin12), .out2(n74175_1_pin5), .out3(n74175_1_pin4), .in(1'b1),
    .sel(random_1_out));
  Demultiplexer #(.select(2)) demultiplexer_2 (
    .out0(n74175_2_pin13), .out1(n74175_2_pin12), .out2(n74175_2_pin5), .out3(n74175_2_pin4), .in(1'b1),
    .sel(random_1_out));
  Demultiplexer #(.select(2)) demultiplexer_3 (
    .out0(n74175_3_pin13), .out1(n74175_3_pin12), .out2(n74175_3_pin5), .out3(n74175_3_pin4), .in(1'b1),
    .sel(random_1_out));
  Demultiplexer #(.select(2)) demultiplexer_4 (
    .out0(n74175_4_pin13), .out1(n74175_4_pin12), .out2(n74175_4_pin5), .out3(n74175_4_pin4), .in(1'b1),
    .sel(random_1_out));
  Demultiplexer #(.select(2)) demultiplexer_5 (
    .out0(n74175_5_pin13), .out1(n74175_5_pin12), .out2(n74175_5_pin5), .out3(n74175_5_pin4), .in(1'b1),
    .sel(random_1_out));
  Multiplexer #(.select(3)) multiplexer_7 (
    .in0(n74175_1_pin7), .in1(n74175_2_pin7), .in2(n74175_3_pin7), .in3(n74175_4_pin7), .in4(n74175_5_pin7),
    .in5(1'b0), .in6(1'b0), .in7(1'b0), .out(multiplexer_7_out), .sel(counter_1_q));
  Multiplexer #(.select(3)) multiplexer_8 (
    .in0(n74175_1_pin2), .in1(n74175_2_pin2), .in2(n74175_3_pin2), .in3(n74175_4_pin2), .in4(n74175_5_pin2),
    .in5(1'b0), .in6(1'b0), .in7(1'b0), .out(multiplexer_8_out), .sel(counter_1_q));
  Multiplexer #(.select(3)) multiplexer_9 (
    .in0(n74175_1_pin15), .in1(n74175_2_pin15), .in2(n74175_3_pin15), .in3(n74175_4_pin15),
    .in4(n74175_5_pin15), .in5(1'b0), .in6(1'b0), .in7(1'b0), .out(multiplexer_9_out), .sel(counter_1_q));
  Multiplexer #(.select(3)) multiplexer_10 (
    .in0(n74175_1_pin10), .in1(n74175_2_pin10), .in2(n74175_3_pin10), .in3(n74175_4_pin10),
    .in4(n74175_5_pin10), .in5(1'b0), .in6(1'b0), .in7(1'b0), .out(multiplexer_10_out), .sel(counter_1_q));
  Demultiplexer #(.select(3)) demultiplexer_6 (
    .out0(demultiplexer_6_out0), .out1(n74175_2_pin9), .out2(n74175_3_pin9), .out3(n74175_4_pin9),
    .out4(n74175_5_pin9), .out6(demultiplexer_6_out6), .out7(demultiplexer_6_out7), .in(or_10_out),
    .sel(counter_2_q));  // open: out5
  or or_12 (or_12_out, n74175_5_pin9, n74175_4_pin9, n74175_3_pin9, n74175_2_pin9);
  Clock clock_4 (.out(clock_4_out));
  Random #(.width(2)) random_1 (.next(1'b1), .clk(clock_4_out), .out(random_1_out));  // open: clr

  // Notes on the sheet:
  //   some delay before show 
  //   show until there is no data yet
  //   show all button that you must press
  //   this is counter (ic)
  //   User
  //   compare if current state hit max
  //   will go next state if release button
  //   Simon
  //   Max count
  //   current state
  //   correct
  //   Dont Forget to TURN ON Clock
  //   it wil count first pressed
  //   prevent some kids press all button,
  //   Nah
  //   Start Game
  //   still do nothing if you press wrong button
  //   give me idea plz faii, im depressed
  //   Reset Data
  //   Reset
  //   Memory 4bits * 8 => 32 bits
  //   Random
endmodule
